// Logisim project 22-Bit MIPS.circ as structural Verilog: 5 circuits, main circuit datapath
module Register_File (
  input  [4:0] in_1,
  input  [4:0] in_2,
  input  [4:0] in_3,
  input  Clk,
  input  Clear,
  input  Write_Control,
  input  [21:0] Write_Data,
  output [21:0] Output_1,
  output [21:0] Output_2
);

  wire and_1_out, and_2_out, and_3_out, and_4_out, and_5_out, and_6_out, and_7_out, and_8_out, and_9_out,
       and_10_out, and_11_out, and_12_out, and_13_out, and_14_out, and_15_out, and_16_out, and_17_out,
       and_18_out, and_19_out, and_20_out, and_21_out, and_22_out, decoder_1_out0, decoder_1_out1,
       decoder_1_out2, decoder_1_out3, decoder_1_out4, decoder_1_out5, decoder_1_out6, decoder_1_out7,
       decoder_1_out8, decoder_1_out9, decoder_1_out10, decoder_1_out11, decoder_1_out12, decoder_1_out13,
       decoder_1_out14, decoder_1_out15, decoder_1_out16, decoder_1_out17, decoder_1_out18, decoder_1_out19,
       decoder_1_out20, decoder_1_out21;
  wire [21:0] R0_q, R1_q, R2_q, R3_q, R4_q, R5_q, R6_q, R7_q, R8_q, R9_q, R10_q, R11_q, R12_q, R13_q, R14_q,
       R15_q, R16_q, R17_q, R18_q, R19_q, R20_q, R21_q;

  Decoder #(.select(5), .enable("false")) decoder_1 (
    .out0(decoder_1_out0), .out1(decoder_1_out1), .out2(decoder_1_out2), .out3(decoder_1_out3),
    .out4(decoder_1_out4), .out5(decoder_1_out5), .out6(decoder_1_out6), .out7(decoder_1_out7),
    .out8(decoder_1_out8), .out9(decoder_1_out9), .out10(decoder_1_out10), .out11(decoder_1_out11),
    .out12(decoder_1_out12), .out13(decoder_1_out13), .out14(decoder_1_out14), .out15(decoder_1_out15),
    .out16(decoder_1_out16), .out17(decoder_1_out17), .out18(decoder_1_out18), .out19(decoder_1_out19),
    .out20(decoder_1_out20), .out21(decoder_1_out21), .sel(in_1));  // open: out22, out23, out24, out25, out26, out27, out28, out29, out30, out31
  Register #(.width(22)) R0 (.D(Write_Data), .en(and_1_out), .Q(R0_q), .clk(Clk), .clr(Clear));
  and and_1 (and_1_out, decoder_1_out0, Write_Control);
  Register #(.width(22)) R1 (.D(Write_Data), .en(and_2_out), .Q(R1_q), .clk(Clk), .clr(Clear));
  and and_2 (and_2_out, decoder_1_out1, Write_Control);
  Register #(.width(22)) R2 (.D(Write_Data), .en(and_3_out), .Q(R2_q), .clk(Clk), .clr(Clear));
  and and_3 (and_3_out, decoder_1_out2, Write_Control);
  Register #(.width(22)) R3 (.D(Write_Data), .en(and_4_out), .Q(R3_q), .clk(Clk), .clr(Clear));
  and and_4 (and_4_out, decoder_1_out3, Write_Control);
  Register #(.width(22)) R4 (.D(Write_Data), .en(and_5_out), .Q(R4_q), .clk(Clk), .clr(Clear));
  and and_5 (and_5_out, decoder_1_out4, Write_Control);
  Register #(.width(22)) R5 (.D(Write_Data), .en(and_6_out), .Q(R5_q), .clk(Clk), .clr(Clear));
  and and_6 (and_6_out, decoder_1_out5, Write_Control);
  Register #(.width(22)) R6 (.D(Write_Data), .en(and_7_out), .Q(R6_q), .clk(Clk), .clr(Clear));
  and and_7 (and_7_out, decoder_1_out6, Write_Control);
  Register #(.width(22)) R7 (.D(Write_Data), .en(and_8_out), .Q(R7_q), .clk(Clk), .clr(Clear));
  and and_8 (and_8_out, decoder_1_out7, Write_Control);
  Register #(.width(22)) R8 (.D(Write_Data), .en(and_9_out), .Q(R8_q), .clk(Clk), .clr(Clear));
  and and_9 (and_9_out, decoder_1_out8, Write_Control);
  Register #(.width(22)) R9 (.D(Write_Data), .en(and_10_out), .Q(R9_q), .clk(Clk), .clr(Clear));
  and and_10 (and_10_out, decoder_1_out9, Write_Control);
  Register #(.width(22)) R10 (.D(Write_Data), .en(and_11_out), .Q(R10_q), .clk(Clk), .clr(Clear));
  and and_11 (and_11_out, decoder_1_out10, Write_Control);
  and and_12 (and_12_out, decoder_1_out11, Write_Control);
  and and_13 (and_13_out, decoder_1_out12, Write_Control);
  and and_14 (and_14_out, decoder_1_out13, Write_Control);
  and and_15 (and_15_out, decoder_1_out14, Write_Control);
  and and_16 (and_16_out, decoder_1_out15, Write_Control);
  and and_17 (and_17_out, decoder_1_out16, Write_Control);
  and and_18 (and_18_out, decoder_1_out17, Write_Control);
  and and_19 (and_19_out, decoder_1_out18, Write_Control);
  and and_20 (and_20_out, decoder_1_out19, Write_Control);
  and and_21 (and_21_out, decoder_1_out20, Write_Control);
  and and_22 (and_22_out, decoder_1_out21, Write_Control);
  Register #(.width(22)) R11 (.D(Write_Data), .en(and_12_out), .Q(R11_q), .clk(Clk), .clr(Clear));
  Register #(.width(22)) R12 (.D(Write_Data), .en(and_13_out), .Q(R12_q), .clk(Clk), .clr(Clear));
  Register #(.width(22)) R13 (.D(Write_Data), .en(and_14_out), .Q(R13_q), .clk(Clk), .clr(Clear));
  Register #(.width(22)) R14 (.D(Write_Data), .en(and_15_out), .Q(R14_q), .clk(Clk), .clr(Clear));
  Register #(.width(22)) R15 (.D(Write_Data), .en(and_16_out), .Q(R15_q), .clk(Clk), .clr(Clear));
  Register #(.width(22)) R16 (.D(Write_Data), .en(and_17_out), .Q(R16_q), .clk(Clk), .clr(Clear));
  Register #(.width(22)) R17 (.D(Write_Data), .en(and_18_out), .Q(R17_q), .clk(Clk), .clr(Clear));
  Register #(.width(22)) R18 (.D(Write_Data), .en(and_19_out), .Q(R18_q), .clk(Clk), .clr(Clear));
  Register #(.width(22)) R19 (.D(Write_Data), .en(and_20_out), .Q(R19_q), .clk(Clk), .clr(Clear));
  Register #(.width(22)) R20 (.D(Write_Data), .en(and_21_out), .Q(R20_q), .clk(Clk), .clr(Clear));
  Register #(.width(22)) R21 (.D(Write_Data), .en(and_22_out), .Q(R21_q), .clk(Clk), .clr(Clear));
  Multiplexer #(.select(5), .width(22), .enable("false")) multiplexer_1 (
    .in0(R0_q), .in1(R1_q), .in2(R2_q), .in3(R3_q), .in4(R4_q), .in5(R5_q), .in6(R6_q), .in7(R7_q),
    .in8(R8_q), .in9(R9_q), .in10(R10_q), .in11(R11_q), .in12(R12_q), .in13(R13_q), .in14(R14_q),
    .in15(R15_q), .in16(R16_q), .in17(R17_q), .in18(R18_q), .in19(R19_q), .in20(R20_q), .in21(R21_q),
    .out(Output_1), .sel(in_2));  // open: in22, in23, in24, in25, in26, in27, in28, in29, in30, in31
  Multiplexer #(.select(5), .width(22), .enable("false")) multiplexer_2 (
    .in0(R0_q), .in1(R1_q), .in2(R2_q), .in3(R3_q), .in4(R4_q), .in5(R5_q), .in6(R6_q), .in7(R7_q),
    .in8(R8_q), .in9(R9_q), .in10(R10_q), .in11(R11_q), .in12(R12_q), .in13(R13_q), .in14(R14_q),
    .in15(R15_q), .in16(R16_q), .in17(R17_q), .in18(R18_q), .in19(R19_q), .in20(R20_q), .in21(R21_q),
    .out(Output_2), .sel(in_3));  // open: in22, in23, in24, in25, in26, in27, in28, in29, in30, in31
endmodule

module ALU_minimized (
  input  [21:0] A,
  input  [21:0] B,
  input  [2:0] ALU_Control,
  output [21:0] out_4,
  output BNE,
  output BEQ
);

  wire comparator_1_lt;
  wire [21:0] adder_1_out, and_1_out, bit_extender_1_out, nor_1_out, or_1_out, shifter_1_out, shifter_2_out,
       subtractor_1_out;

  Shifter #(.width(22)) shifter_1 (.in(A), .\dist (5'b00001), .out(shifter_1_out));
  Shifter #(.width(22), .shift("lr")) shifter_2 (.in(A), .\dist (5'b00001), .out(shifter_2_out));
  Adder #(.width(22)) adder_1 (.a(A), .b(B), .out(adder_1_out), .cin(1'b0));  // open: cout
  assign or_1_out = A | B;  // OR_Gate or_1, 22 bits wide
  assign nor_1_out = ~(A | B);  // NOR_Gate nor_1, 22 bits wide
  assign and_1_out = A & B;  // AND_Gate and_1, 22 bits wide
  Subtractor #(.width(22)) subtractor_1 (.a(A), .b(B), .out(subtractor_1_out), .bin(1'b0));  // open: bout
  Comparator #(.width(22)) comparator_1 (.a(A), .b(B), .eq(BEQ), .lt(comparator_1_lt));  // open: gt
  assign bit_extender_1_out = {{21{1'b0}}, comparator_1_lt};  // Bit_Extender bit_extender_1
  not not_1 (BNE, BEQ);
  Multiplexer #(.select(3), .width(22), .enable("false")) multiplexer_1 (
    .in0(shifter_1_out), .in1(shifter_2_out), .in2(adder_1_out), .in3(or_1_out), .in4(nor_1_out),
    .in5(and_1_out), .in6(subtractor_1_out), .in7(bit_extender_1_out), .out(out_4), .sel(ALU_Control));

  // Notes on the sheet:
  //   SLL
  //   SRL
  //   ADD
  //   OR
  //   NOR
  //   AND
  //   SUB
  //   SLT
  //   ALU Out
endmodule

module ControlUnit (
  input  [3:0] OPCode,
  output RegWrite,
  output RegDest,
  output ALU_SRC,
  output Branch,
  output MemWrite,
  output MemRead,
  output MemToReg,
  output ALUOP1,
  output ALU_OP_0,
  output Jump
);

  wire decoder_1_out1, decoder_1_out2, decoder_1_out4;

  Decoder #(.select(4), .disabled(0), .enable("false")) decoder_1 (
    .out0(ALUOP1), .out1(decoder_1_out1), .out2(decoder_1_out2), .out4(decoder_1_out4), .out5(MemRead),
    .out6(MemWrite), .out7(Jump), .sel(OPCode));  // open: out3, out8, out9, out10, out11, out12, out13, out14, out15
  or or_1 (RegWrite, ALUOP1, decoder_1_out4, MemRead);
  or or_2 (ALU_SRC, decoder_1_out4, MemRead, MemWrite);
  or or_3 (Branch, decoder_1_out1, decoder_1_out2);
  or or_4 (ALU_OP_0, decoder_1_out1, decoder_1_out2);

  assign MemToReg = MemRead;
  assign RegDest = ALUOP1;
endmodule

module datapath (
  input  in_1,
  input  in_2,
  input  in_3
);

  wire ALU_beq, ALU_bne, ALUOP0, ALUOP1, and_1_out, and_2_out, BNE, clock_1_out, Control_Unit_alu_src,
       Control_Unit_branch, Control_Unit_jump, Control_Unit_memread, Control_Unit_memtoreg,
       Control_Unit_memwrite, Control_Unit_regdest, Control_Unit_regwrite, or_1_out;
  wire [2:0] ALU_Control_alucontrol0;
  wire [4:0] multiplexer_1_out;
  wire [21:0] adder_1_out, adder_2_out, ALU_out_4, bit_extender_2_out, imm, multiplexer_2_out,
       multiplexer_3_out, multiplexer_4_out, multiplexer_5_out, PC_q, ram_1_data, Registers_output_1,
       Registers_output_2, rom_1_data;

  Register #(.width(22)) PC (.D(multiplexer_4_out), .Q(PC_q), .clk(clock_1_out), .clr(in_1));  // open: en
  Clock clock_1 (.out(clock_1_out));
  Adder #(.width(22)) adder_1 (.a(22'h1), .b(PC_q), .out(adder_1_out));  // open: cin, cout
  ROM #(.addrWidth(22), .dataWidth(22)) rom_1 (
    .addr(PC_q), .data({rom_1_data[21:19], BNE, rom_1_data[17:0]}));  // open: sel
  assign imm = {{14{1'b0}}, rom_1_data[7:0]};  // Bit_Extender bit_extender_1
  assign bit_extender_2_out = {{4{1'b0}}, rom_1_data[17:0]};  // Bit_Extender bit_extender_2
  Multiplexer #(.width(5), .enable("false")) multiplexer_1 (
    .in0(rom_1_data[12:8]), .in1(rom_1_data[7:3]), .out(multiplexer_1_out), .sel(Control_Unit_regdest));
  ControlUnit Control_Unit (
    .OPCode({rom_1_data[21:19], BNE}), .RegWrite(Control_Unit_regwrite), .RegDest(Control_Unit_regdest),
    .ALU_SRC(Control_Unit_alu_src), .Branch(Control_Unit_branch), .MemWrite(Control_Unit_memwrite),
    .MemRead(Control_Unit_memread), .MemToReg(Control_Unit_memtoreg), .ALUOP1(ALUOP1), .ALU_OP_0(ALUOP0),
    .Jump(Control_Unit_jump));
  Register_File Registers (
    .Output_1(Registers_output_1), .Output_2(Registers_output_2), .in_1(multiplexer_1_out), .Clear(in_2),
    .Write_Control(Control_Unit_regwrite), .Write_Data(multiplexer_5_out), .in_2(rom_1_data[17:13]),
    .in_3(rom_1_data[12:8]), .Clk(clock_1_out));
  Adder #(.width(22)) adder_2 (.a(adder_1_out), .b(imm), .out(adder_2_out));  // open: cin, cout
  or or_1 (or_1_out, and_1_out, and_2_out);
  and and_1 (and_1_out, Control_Unit_branch, ALU_beq);
  and and_2 (and_2_out, Control_Unit_branch, BNE, ALU_bne);
  Multiplexer #(.width(22), .enable("false")) multiplexer_2 (
    .in0(Registers_output_2), .in1(imm), .out(multiplexer_2_out), .sel(Control_Unit_alu_src));
  ALU_Control ALU_Control (
    .ALUControl0(ALU_Control_alucontrol0[0]), .ALUControl1(ALU_Control_alucontrol0[1]),
    .ALUControl2(ALU_Control_alucontrol0[2]), .FuncBits(rom_1_data[2:0]), .ALUOp({ALUOP1, ALUOP0}),
    .OPCODE({rom_1_data[21:19], BNE}));
  Multiplexer #(.width(22), .enable("false")) multiplexer_3 (
    .in0(adder_1_out), .in1(adder_2_out), .out(multiplexer_3_out), .sel(or_1_out));
  ALU_minimized ALU (
    .out_4(ALU_out_4), .BNE(ALU_bne), .A(Registers_output_1), .B(multiplexer_2_out), .BEQ(ALU_beq),
    .ALU_Control(ALU_Control_alucontrol0));
  Multiplexer #(.width(22), .enable("false")) multiplexer_4 (
    .in0(multiplexer_3_out), .in1(bit_extender_2_out), .out(multiplexer_4_out), .sel(Control_Unit_jump));
  RAM #(.addrWidth(22), .dataWidth(22), .bus("separate")) ram_1 (
    .addr(ALU_out_4), .din(Registers_output_2), .data(ram_1_data), .str(Control_Unit_memwrite),
    .clk(clock_1_out), .ld(Control_Unit_memread), .clr(in_3));  // open: sel
  Multiplexer #(.width(22), .enable("false")) multiplexer_5 (
    .in0(ALU_out_4), .in1(ram_1_data), .out(multiplexer_5_out), .sel(Control_Unit_memtoreg));

  // Notes on the sheet:
  //   contents of rom_1 (hex, n*v repeats v):
  //   100105 10020a 10030f 100414 2229 6135 223c 2342 224b 2256 6158 2367 84102 0 44102 0 102d19 180d64
  //   140e64 1c000a
  //   address
  //   imm.
  //   func bits
  //   rd
  //   rt
  //   rs
  //   opcode
endmodule

module ALU_Control (
  input  [3:0] OPCODE,
  input  [2:0] FuncBits,
  input  [1:0] ALUOp,
  output ALUControl0,
  output ALUControl1,
  output ALUControl2
);

  wire ADD_out, ADDi_out, AND_out, BEQ_out, BNE_out, decoder_1_out0, decoder_1_out1, decoder_1_out2,
       decoder_1_out3, decoder_1_out4, decoder_1_out5, decoder_1_out6, decoder_1_out7, decoder_2_out0,
       decoder_2_out1, decoder_2_out2, decoder_2_out3, decoder_3_out0, decoder_3_out1, decoder_3_out2,
       decoder_3_out3, decoder_3_out4, decoder_3_out5, decoder_3_out6, decoder_3_out7, JMP_out, LW_out,
       NOP_out, NOR_out, OR_out, SLL_out, SLT_out, SRL_out, SUB_out, SW_out;

  Decoder #(.select(3), .enable("false")) decoder_1 (
    .out0(decoder_1_out0), .out1(decoder_1_out1), .out2(decoder_1_out2), .out3(decoder_1_out3),
    .out4(decoder_1_out4), .out5(decoder_1_out5), .out6(decoder_1_out6), .out7(decoder_1_out7), .sel(FuncBits));
  Decoder #(.select(2), .enable("false")) decoder_2 (
    .out0(decoder_2_out0), .out1(decoder_2_out1), .out2(decoder_2_out2), .out3(decoder_2_out3), .sel(ALUOp));
  Decoder #(.select(4), .enable("false")) decoder_3 (
    .out0(decoder_3_out0), .out1(decoder_3_out1), .out2(decoder_3_out2), .out3(decoder_3_out3),
    .out4(decoder_3_out4), .out5(decoder_3_out5), .out6(decoder_3_out6), .out7(decoder_3_out7), .sel(OPCODE));  // open: out8, out9, out10, out11, out12, out13, out14, out15
  and SRL (SRL_out, decoder_1_out0, decoder_2_out2, decoder_3_out0);
  and ADD (ADD_out, decoder_1_out1, decoder_2_out2, decoder_3_out0);
  and OR (OR_out, decoder_1_out2, decoder_2_out2, decoder_3_out0);
  and NOR (NOR_out, decoder_1_out3, decoder_2_out2, decoder_3_out0);
  and SUB (SUB_out, decoder_1_out5, decoder_2_out2, decoder_3_out0);
  and SLL (SLL_out, decoder_1_out6, decoder_2_out2, decoder_3_out0);
  and SLT (SLT_out, decoder_1_out7, decoder_2_out1, decoder_3_out0);
  buf BNE (BNE_out, decoder_3_out1);  // AND_Gate
  buf BEQ (BEQ_out, decoder_3_out2);  // AND_Gate
  buf NOP (NOP_out, decoder_3_out3);  // AND_Gate
  buf ADDi (ADDi_out, decoder_3_out4);  // AND_Gate
  buf LW (LW_out, decoder_3_out5);  // AND_Gate
  and AND (AND_out, decoder_1_out4, decoder_2_out2);
  buf JMP (JMP_out, decoder_3_out7);  // AND_Gate
  buf SW (SW_out, decoder_3_out6);  // AND_Gate
  or or_2 (ALUControl0, SRL_out, OR_out, AND_out, SLT_out);
  or or_3 (ALUControl1, SW_out, ADDi_out, ADD_out, OR_out, SUB_out, SLT_out, BNE_out, BEQ_out, LW_out);
  or or_4 (ALUControl2, NOR_out, AND_out, SUB_out, SLT_out, BNE_out, BEQ_out);
endmodule
